# Fritzing sketch guerra_galaxias (saved by Fritzing 0.9.3b)
breadboards: 1

parts:
  Componente1 = Arduino Nano (Rev3.0)
  J1 = Piezo Speaker

nets:
  N1: Componente1.GND, J1.pin1
  N2: Componente1.D11/MOSI, J1.pin2

// code stored in the sketch: Untitled.ino
void setup(){
    pinMode(11,OUTPUT);
}

void loop(){
    
    tone(11,349,500); // write to buzzer
    delay(500);
    tone(11,349,500); // write to buzzer
    delay(500);
    tone(11,349,500); // write to buzzer
    delay(500);
    tone(11,294,250); // write to buzzer
    delay(250);
    tone(11,440,250); // write to buzzer
    delay(250);
    tone(11,349,500); // write to buzzer
    delay(500);
    tone(11,294,250); // write to buzzer
    delay(250);
    tone(11,440,250); // write to buzzer
    delay(250);
    tone(11,349,500); // write to buzzer
    delay(500);
    delay(500);
    tone(11,523,500); // write to buzzer
    delay(500);
    tone(11,523,500); // write to buzzer
    delay(500);
    tone(11,523,500); // write to buzzer
    delay(500);
    tone(11,523,250); // write to buzzer
    delay(250);
    tone(11,440,250); // write to buzzer
    delay(250);
    tone(11,349,500); // write to buzzer
    delay(500);
    tone(11,294,250); // write to buzzer
    delay(250);
    tone(11,440,250); // write to buzzer
    delay(250);
    tone(11,349,500); // write to buzzer
    delay(500);
    delay(500);
}
