# Fritzing sketch intensidad_luz (saved by Fritzing 0.9.3b)
breadboards: 1

parts:
  LED1 = RGB LED (com. cathode, rgb) [package="5 mm [THT]"]
  Componente1 = Arduino Nano (Rev3.0)

nets:
  N1: LED1.common_cathode, Componente1.GND
  N2: LED1.green_anode, Componente1.D5
