# Fritzing sketch luces_aleatorias (saved by Fritzing 0.9.3b)
breadboards: 1

parts:
  LED1 = RGB LED (com. cathode, rgb) [package="5 mm [THT]"]
  Componente1 = Arduino Nano (Rev3.0)

nets:
  N1: LED1.red_anode, Componente1.D6
  N2: LED1.common_cathode, Componente1.GND
  N3: LED1.green_anode, Componente1.D5
  N4: LED1.blue_anode, Componente1.D3
